# Fritzing sketch christmasTreeByNeoPixel (saved by Fritzing 0.9.3b)
breadboards: 1

parts:
  NEOPIXEL1 = Neopixel Strip -- Black (30/m)
  부품1 = Arduino Nano (Rev3.0) (ICSP)
  VCC2 = Battery
  VCC3 = Battery

nets:
  GND: NEOPIXEL1.GND, 부품1.GND, VCC2.-
  N1: NEOPIXEL1.Din, 부품1.D6
  N2: NEOPIXEL1.+5V, VCC3.+
  N3: VCC2.+, VCC3.-

custom parts:
  Neopixel Strip -- Black (30/m): These NeoPixel strips have 30 digitally-addressable pixel LEDs per meter and are very affordable and are only 12.5 mm wide, 10 mm if you remove the strip from the casing.
